# Fritzing sketch RoboticArmV2 (saved by Fritzing 0.9.3b)
breadboards: 1

parts:
  Part1 = Arduino Uno (Rev3)
  Part2 = 16-Channel 12-bit PWM Servo Driver - I2C [part_number=815]
  IC1 = MCP3008 8-channel 10-bit ADC [part_number=MCP3008]
  Part3 = Thumb Joystick
  Part4 = Thumb Joystick
  Part5 = Thumb Joystick
  Part6 = Adafruit I2C+SPI LCD Backpack [part_number="Adafruit #292"]
  LED1 = RGB LED (com. cathode, rbg) [package="5 mm [THT]"]
  R1 = Resistor [tolerance=±5% resistance=220 package=THT]

nets:
  N1: Part1.A4/SDA, Part2.SCL, Part6.CLOCK
  N2: Part1.A5/SCL, Part2.SDA, Part6.DATA
  N3: Part1.D11_PWM/MOSI, IC1.no_name_yet#11
  N4: Part1.D12/MISO, IC1.no_name_yet#12
  GND: Part1.GND, Part2.GND, IC1.no_name_yet#9, IC1.no_name_yet#14, Part3.GND, Part4.GND, Part5.GND, Part6.GND, R1.Pin_0
  N5: Part1.D5_PWM, LED1.blue_anode
  N6: Part1.D6_PWM, LED1.green_anode
  N7: Part1.D7, LED1.red_anode
  VCC: Part1.5V, Part2.5.0V, Part2.VCC, IC1.no_name_yet#15, IC1.no_name_yet#16, Part3.VCC, Part4.VCC, Part5.VCC, Part6.VCC
  N8: IC1.no_name_yet#1, Part3.VERT
  N9: IC1.no_name_yet#2, Part3.HORZ
  N10: IC1.no_name_yet#3, Part4.VERT
  N11: IC1.no_name_yet#4, Part4.HORZ
  N12: IC1.no_name_yet#5, Part5.VERT
  N13: IC1.no_name_yet#6, Part5.HORZ
  N14: LED1.common_cathode, R1.Pin_1

custom parts:
  16-Channel 12-bit PWM Servo Driver - I2C: You want to make a cool robot, maybe a hexapod walker, or maybe just a piece of art with a lot of moving parts. Or maybe you want to drive a lot of LEDs with precise PWM output. Using only two pins, control 16 free-running PWM outputs! You can even chain up 62 breakouts to control up to 992 PWM outputs.
  Adafruit I2C+SPI LCD Backpack: LCD backpacks reduce the number of pins needed to connect to an LCD. LCDs are a fun and easy way to have your microcontroller project talk back to you. Character LCDs are common, and easy to get, available in tons of colors and sizes. We've written tutorials on using character LCDs with an Arduino (or similar microcontroller) but find that the number of pins necessary to control the LCD can be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
